// Logisim project LabArqui.circ as structural Verilog: 1 circuit, main circuit main
module main (
  input  A,
  input  B,
  output Mayor,
  output Igual,
  output Menor
);

  wire not_1_out, not_2_out, or_1_out;

  not not_1 (not_1_out, B);
  not not_2 (not_2_out, A);
  and and_1 (Mayor, A, not_1_out);
  buf and_2 (Menor, not_2_out);  // AND_Gate
  or or_1 (or_1_out, Mayor, Menor);
  not not_3 (Igual, or_1_out);
endmodule
